// Logisim project ALU_4Bit.circ as structural Verilog: 7 circuits, main circuit FA-1Bit
module FA_1Bit (
  input  A,
  input  B,
  input  Cin,
  output Sum,
  output Cout
);

  wire and_1_out, and_2_out, xor_2_out;

  ExactlyOne xor_1 (.out(Sum), .in1(A), .in2(B), .in3(Cin));
  and and_1 (and_1_out, A, B);
  xor xor_2 (xor_2_out, A, B);
  and and_2 (and_2_out, Cin, xor_2_out);
  or or_1 (Cout, and_1_out, and_2_out);
endmodule

module AU (
  input  Cin,
  input  A0,
  input  A1,
  input  A2,
  input  A3,
  input  B0,
  input  B1,
  input  B2,
  input  B3,
  output [3:0] Result,
  output Cout
);

  wire fa_1bit_1_cout, fa_1bit_2_cout, fa_1bit_3_cout, xor_1_out, xor_2_out, xor_3_out, xor_4_out;

  xor xor_1 (xor_1_out, Cin, B0);
  xor xor_2 (xor_2_out, Cin, B1);
  xor xor_3 (xor_3_out, Cin, B2);
  xor xor_4 (xor_4_out, Cin, B3);
  FA_1Bit fa_1bit_1 (.A(A0), .B(xor_1_out), .Cin(Cin), .Sum(Result[0]), .Cout(fa_1bit_1_cout));
  FA_1Bit fa_1bit_2 (.A(A1), .B(xor_2_out), .Cin(fa_1bit_1_cout), .Sum(Result[1]), .Cout(fa_1bit_2_cout));
  FA_1Bit fa_1bit_3 (.A(A2), .B(xor_3_out), .Cin(fa_1bit_2_cout), .Sum(Result[2]), .Cout(fa_1bit_3_cout));
  FA_1Bit fa_1bit_4 (.A(A3), .B(xor_4_out), .Cin(fa_1bit_3_cout), .Sum(Result[3]), .Cout(Cout));
endmodule

module Logic_Unit (
  input  S1,
  input  S0,
  input  A0,
  input  B0,
  input  A1,
  input  B1,
  input  A2,
  input  B2,
  input  A3,
  input  B3,
  output [3:0] Result
);

  wire and_1_out, and_2_out, and_3_out, and_4_out, not_1_out, not_2_out, not_3_out, not_4_out, or_1_out,
       or_2_out, or_3_out, or_4_out, xor_1_out, xor_2_out, xor_3_out, xor_4_out;

  not not_1 (not_1_out, A0);
  not not_2 (not_2_out, A1);
  not not_3 (not_3_out, A2);
  not not_4 (not_4_out, A3);
  and and_1 (and_1_out, A0, B0);
  or or_1 (or_1_out, A0, B0);
  xor xor_1 (xor_1_out, A0, B0);
  and and_2 (and_2_out, A1, B1);
  or or_2 (or_2_out, A1, B1);
  xor xor_2 (xor_2_out, A1, B1);
  and and_3 (and_3_out, A2, B2);
  or or_3 (or_3_out, A2, B2);
  xor xor_3 (xor_3_out, A2, B2);
  and and_4 (and_4_out, A3, B3);
  or or_4 (or_4_out, A3, B3);
  xor xor_4 (xor_4_out, A3, B3);
  Multiplexer #(.select(2)) multiplexer_1 (
    .in0(and_1_out), .in1(or_1_out), .in2(xor_1_out), .in3(not_1_out), .out(Result[0]), .sel({S1, S0}));  // open: en
  Multiplexer #(.select(2)) multiplexer_2 (
    .in0(and_2_out), .in1(or_2_out), .in2(xor_2_out), .in3(not_2_out), .out(Result[1]), .sel({S1, S0}));  // open: en
  Multiplexer #(.select(2)) multiplexer_3 (
    .in0(and_3_out), .in1(or_3_out), .in2(xor_3_out), .in3(not_3_out), .out(Result[2]), .sel({S1, S0}));  // open: en
  Multiplexer #(.select(2)) multiplexer_4 (
    .in0(and_4_out), .in1(or_4_out), .in2(xor_4_out), .in3(not_4_out), .out(Result[3]), .sel({S1, S0}));  // open: en
endmodule

module R_shift (
  input  in_0,
  input  in_1,
  input  in_2,
  input  in_3,
  output out_0,
  output out_1,
  output out_2,
  output out_8
);


  assign out_0 = in_1;
  assign out_1 = in_2;
  assign out_2 = in_3;
  assign out_8 = 1'b0;
endmodule

// L-Shift
module L_shift (
  input  in_0,
  input  in_1,
  input  in_2,
  input  in_3,
  output out_0,
  output out_1,
  output out_2,
  output out_3
);


  assign out_0 = 1'b0;
  assign out_1 = in_0;
  assign out_2 = in_1;
  assign out_3 = in_2;
endmodule

module Comparator (
  input  A0,
  input  A1,
  input  A2,
  input  A3,
  input  B0,
  input  B1,
  input  B2,
  input  B3,
  output Greater,
  output Equal,
  output Less
);

  Comparator_part #(.width(4), .mode("unsigned")) comparator_1 (
    .a({A3, A2, A1, A0}), .b({B3, B2, B1, B0}), .gt(Greater), .eq(Equal), .lt(Less));
endmodule

module ALU (
  input  Cin,
  input  S2,
  input  S1,
  input  S0,
  input  A3,
  input  A2,
  input  A1,
  input  A0,
  input  B3,
  input  B2,
  input  B1,
  input  B0,
  input  S1_2,
  input  S0_2,
  output Cout,
  output [3:0] Result,
  output Greater,
  output Equal,
  output Less
);

  wire [3:0] au_1_result, l_shift_1_out_0, logic_unit_1_result, r_shift_1_out_0;

  R_shift r_shift_1 (
    .in_0(A0), .in_1(A1), .in_2(A2), .in_3(A3), .out_0(r_shift_1_out_0[0]), .out_1(r_shift_1_out_0[1]),
    .out_2(r_shift_1_out_0[2]), .out_8(r_shift_1_out_0[3]));
  L_shift l_shift_1 (
    .in_0(A0), .in_1(A1), .in_2(A2), .in_3(A3), .out_0(l_shift_1_out_0[0]), .out_1(l_shift_1_out_0[1]),
    .out_2(l_shift_1_out_0[2]), .out_3(l_shift_1_out_0[3]));
  Comparator comparator_1 (
    .A0(A0), .A1(A1), .A2(A2), .A3(A3), .B0(B0), .B1(B1), .B2(B2), .B3(B3), .Equal(Equal), .Less(Less),
    .Greater(Greater));
  AU au_1 (
    .Cout(Cout), .Cin(Cin), .A0(A0), .A1(A1), .A2(A2), .A3(A3), .B0(B0), .B1(B1), .B2(B2), .B3(B3),
    .Result(au_1_result));
  Logic_Unit logic_unit_1 (
    .A0(A0), .B0(B0), .A1(A1), .B1(B1), .A2(A2), .B2(B2), .A3(A3), .B3(B3), .Result(logic_unit_1_result),
    .S0(S0_2), .S1(S1_2));
  Multiplexer #(.select(3), .width(4), .enable("false")) multiplexer_1 (
    .in0(au_1_result), .in1(logic_unit_1_result), .in2(r_shift_1_out_0), .in3(l_shift_1_out_0),
    .in4(4'b0001), .in5(4'b0010), .in6(4'b0100), .out(Result), .sel({S2, S1, S0}));  // open: in7

  // Notes on the sheet:
  //   Result: pull=up
endmodule
